# Fritzing sketch AutoTea (saved by Fritzing 0.9.3b)
breadboards: 1

parts:
  Part1 = Arduino Mega 2560 (Rev3)
  U2 = LCD-16X2 [package=lcd-16x2]
  S1 = Pushbutton [package="[SMD]"]
  LED1 = RGB LED - (4 legs) [package="5 mm [THT]"]
  U1 = POT [package=pot_alpha_rv16af-20]
  J1 = Basic Servo
  Water_Sensor = hc-sr04
  Cup_Sensor = hc-sr04  # not connected

nets:
  N1: Part1.D13_PWM, Water_Sensor.Trig
  5V: Part1.D12_PWM, Part1.5V, U2.VDD, U2.VO, U2.DB7, U2.A, U1.S, U1.E, J1.vcc
  N2: Part1.D11_PWM, U2.DB6
  N3: Part1.D10_PWM, U2.DB5
  N4: Part1.D9_PWM, U2.DB3, U2.DB4
  N5: Part1.D8_PWM, U2.E, U2.DB0
  GND: Part1.GND, U2.VSS, U2.K, S1.Pin_1, S1.Pin_2, U1.A, J1.gnd
  N6: Part1.D6_PWM, Water_Sensor.Echo
  N7: Part1.D7_PWM, U2.RS, U2.R_W
  N8: Part1.D48, LED1.blue_cathode
  N9: Part1.D50, LED1.green_cathode
  N10: Part1.D51, J1.pulse
  N11: Part1.D52, LED1.red_cathode
  N12: Part1.D53, S1.Pin_3, S1.Pin_4
